// Logisim project L08_Example.circ as structural Verilog: 2 circuits, main circuit main
module main (
  input  [31:0] Integer_variable,
  input  [63:0] in_2,
  input  Sign,
  input  [7:0] Exponent,
  input  [22:0] Mantisa
);

  wire [31:0] F32_TO_Q31_q31_mem;
  wire [63:0] F32_TO_Q31_q31_val;

  Q31 F32_TO_Q31 (.F64(in_2), .Q31_Val(F32_TO_Q31_q31_val), .Q31_Mem(F32_TO_Q31_q31_mem));
  // Probe on Integer_variable
  // Probe on Integer_variable
  // Probe on Integer_variable
  // Probe on F32_TO_Q31_q31_val
  // Probe on F32_TO_Q31_q31_mem
  // Probe on F32_TO_Q31_q31_mem
  // Probe on F32_TO_Q31_q31_mem
  // Probe on {Sign, Exponent, Mantisa}
  // Probe on {Sign, Exponent, Mantisa}
  // Probe on {Sign, Exponent, Mantisa}
  // Probe on Integer_variable
  // Probe on {Sign, Exponent, Mantisa}

  // Notes on the sheet:
  //   Fixed-point variable
  //   Floating-point variable
endmodule

module Q31 (
  input  [63:0] F64,
  output [63:0] Q31_Val,
  output [31:0] Q31_Mem
);

  wire [63:0] fpmultiplier_1_out, inttofp_1_p2, inttofp_2_p2;

  // IntToFP #(.fpwidth(64), .width(64)) inttofp_1: pin names not known; wires that end beside it: 64'h80000000, inttofp_1_p2
  FPDivider #(.fpwidth(64)) fpdivider_1 (.a(inttofp_2_p2), .b(inttofp_1_p2), .out(Q31_Val));
  FPMultiplier #(.fpwidth(64)) fpmultiplier_1 (.a(F64), .b(inttofp_1_p2), .out(fpmultiplier_1_out));
  // FPToInt #(.fpwidth(64), .mode("truncate"), .width(32)) fptoint_1: pin names not known; wires that end beside it: fpmultiplier_1_out, Q31_Mem
  // IntToFP #(.fpwidth(64), .width(32)) inttofp_2: pin names not known; wires that end beside it: Q31_Mem, inttofp_2_p2
endmodule
